# Fritzing sketch ticking bomb (saved by Fritzing 0.9.6b)
circuit board: 8.46667cm x 5.64444cm
breadboards: 1

parts:
  R1 = Resistor [tolerance=±5% power=0.25 resistance=47k package=THT]
  C1 = Ceramic Capacitor [capacitance=10µF voltage=20V package="100 mil [THT, multilayer]"]
  U1 = 555 Timer [package="SO8 [SMD]"]
  C2 = Ceramic Capacitor [capacitance=10µF voltage=20V package="100 mil [THT, multilayer]"]
  SPKR1 = Loudspeaker
  VCC1 = Battery block 9V

nets:
  N1: R1.Pin_0, C1.1, U1.Pin_2, U1.Pin_6
  N2: R1.Pin_1, U1.Pin_4, U1.Pin_8, C2.1, VCC1.+
  N3: C1.0, U1.Pin_1, SPKR1.pin2, VCC1.-
  N4: U1.Pin_3, C2.0, SPKR1.pin1
